# Fritzing sketch shield (saved by Fritzing 0.8.7b)

parts:
  RE1 = KY-040 Rotary encoder [package=THT]
  DS1 = DS18B20 1-Wire Temperature Sensor Probe
  U1 = WS2812 RGB LED matrix 1x8
  U2 = WS2812 RGB LED matrix 1x8
  Part3 = Adafruit Proto Shield for Arduino Kit - v.5
  R1 = Photocell (LDR) [package=THT]
  Part4 = LCD1602-I2C
  LED1 = smd LED [color="Red (633nm)" package="0805 [SMD]"]
  LED2 = smd LED [color="Green (555nm)" package="0805 [SMD]"]
  R2 = Resistor [tolerance=±5% resistance=10k package=THT]
  S2 = Pushbutton [package="[THT]"]
  R3 = Resistor [tolerance=±5% resistance=10k package=THT]
  R5 = Resistor [tolerance=±5% resistance=220 package=THT]
  R6 = Resistor [tolerance=±5% resistance=220 package=THT]
  WeMos_D1_R1 = WeMos D1 R2  # not connected
  R7 = Resistor [tolerance=±5% resistance=10k package=THT]

nets (from the breadboard view):
  GND: RE1.GND, DS1.GND, U1.GND#0, U1.GND#3, Part3.P$7, Part3.GND, Part3.P$8, Part3.P$9#24, Part3.P$10, Part3.P$11#26, Part3.P$12#27, Part3.1, Part3.P$4, Part3.N$10, Part3.N$114, Part3.N$118, Part3.N$218, Part4.GND, LED1.cathode, LED2.cathode, R2.Pin_0, S2.Pin_1, S2.Pin_2, R7.Pin_1
  N1: RE1.DT, Part3.D8
  N2: RE1.CLK, Part3.D9
  N3: DS1.DQ, Part3.D2
  VDD: DS1.VDD, U1.VCC#1, Part3.+5V, Part3.P$9#223, Part3.P$11#225, Part3.P$12#226, R1.pin_1, Part4.VCC, R3.Pin_0
  N4: U1.DIN, Part3.D6
  N5: U1.GND#4, U1.GND#7, U2.GND
  N6: U1.VCC#5, U2.VCC
  N7: U1.DOUT, U2.DIN
  N8: Part3.SOIC5, R6.Pin_1
  N9: Part3.SOIC7, R5.Pin_1
  N10: Part3.D10, Part3.N$66, R5.Pin_0, R7.Pin_0
  N11: Part3.D3, Part3.P$5#147, Part4.SCL
  N12: Part3.D4, Part3.P$5#144, Part4.SDA
  N13: Part3.D5, R6.Pin_0
  N14: Part3.D7, Part3.N$24, Part3.N$123, S2.Pin_3, S2.Pin_4
  N15: Part3.A5, R1.pin_0, R2.Pin_1
  N16: Part3.N$9, LED2.anode
  N17: Part3.N$42, LED1.anode

notes:
  červená LED = D8 / GPIO15
  button = D5
  na prototype součástce nelze spojit

custom parts:
  KY-040 Rotary encoder: KY-040 Rotary Encoder with switch on breakout borad from AZ Delivery
  WS2812 RGB LED matrix 1x8: WS2812 matrix 1x8
  Adafruit Proto Shield for Arduino Kit - v.5: Arduino prototyping shield designed by Adafruit Industries
  LCD1602-I2C: A standard character display, usually with 2x16 characters. Comes in many colors with LCM1602 IIC attached.
  WeMos D1 R2: The D1 R2 is a mini wifi board based on the ESP-8266EX.
